# Fritzing sketch skema (saved by Fritzing 0.8.7b)

parts:
  U1 = ESP8266 NodeMCU LoLin module
  LCM1602_IIC2 = LCM1602 IIC [part_number="LCM1602 IIC" chip_label="LCM1602 IIC" package="DIP (Dual Inline) [THT]"]
  U2 = LCD-16X2 [package=lcd-16x2]
  U3 = SWITCH_SPDT [package=kps-1290]
  IC1 = Voltage Regulator [package=78xxl]
  Part4 = adafruit [part_number="Adafruit #4648"]
  C2 = Electrolytic Capacitor [capacitance=100µF package="200 mil [THT, electrolytic]"]
  J1 = Infrared Proximity Sensor
  VCC1 = Battery block 9V

nets:
  N1: U1.D1, LCM1602_IIC2.SCL
  N2: U1.D2, LCM1602_IIC2.SDA
  VSS: LCM1602_IIC2.VSS, U2.VSS
  N3: LCM1602_IIC2.V0, U2.VO
  N4: LCM1602_IIC2.RS, U2.RS
  N5: LCM1602_IIC2.RW, U2.R_W
  N6: LCM1602_IIC2.E, U2.E
  N7: LCM1602_IIC2.D0, U2.DB0
  N8: LCM1602_IIC2.D1, U2.DB1
  N9: LCM1602_IIC2.D2, U2.DB2
  N10: LCM1602_IIC2.D3, U2.DB3
  N11: LCM1602_IIC2.D4, U2.DB4
  N12: LCM1602_IIC2.D5, U2.DB5
  N13: LCM1602_IIC2.D6, U2.DB6
  N14: LCM1602_IIC2.D7, U2.DB7
  N15: LCM1602_IIC2.A, U2.A
  N16: LCM1602_IIC2.K, U2.K
  N17: LCM1602_IIC2.VCC, IC1.OUT
  N18: LCM1602_IIC2.LED_A, LCM1602_IIC2.LED_B
  N19: U3.O, VCC1.+
  N20: U3.P, IC1.IN
  N21: IC1.GND, VCC1.-
  N22: Part4.connector51, J1.Vout
  N23: C2.-, J1.GND

notes:
  Elco 10uF
  Saklar
  Regulator 5v LM7805
  Battery 9v
  PCF8591
  LCD 16x2
  LCD to I2C Adapter
  NodeMCU ESP8266
  SHARP GP2Y0A710K0F

custom parts:
  ESP8266 NodeMCU LoLin module: ESP8266 based NodeMCU
  LCM1602 IIC: I2C-Module to use a 1602 or 2004 LCD on with the wire.h libory Serial LCD Modul
